# Fritzing sketch 1pcb (saved by Fritzing 0.9.3b)

parts:
  U1 = NodeMCU V1.0
  DS1 = DS18B20 1-Wire Temperature Sensor Probe
  DS2 = DS18B20 1-Wire Temperature Sensor Probe
  Part1 = FC-28 Soil Hygrometer Module
  Part2 = FC-28 Soil Hygrometer Module - Probe
  Part3 = LCD1602-I2C
  WATER_PUMP1 = water pump/motor
  KF-1 = KF-301 Relay [package=THT]
  IC1 = MQ-2 [package="DIP (Dual Inline) [THT]"]
  Part6 = ADS1115
  AMS1 = AMS1777 5V regulator module
  Part7 = FC-28 Soil Hygrometer Module
  Part8 = FC-28 Soil Hygrometer Module - Probe
  R1 = Resistor [tolerance=±5% resistance=4.7k package="0402 [SMD]"]
  VCC2 = Battery

nets:
  N1: U1.D1, Part3.SCL, Part6.SCL
  N2: U1.D2, Part3.SDA, Part6.SDA
  N3: U1.D4, DS1.DQ, DS2.DQ, R1.Pin_1
  VDD: U1.3V3, DS1.VDD, DS2.VDD, R1.Pin_0
  GND: U1.GND, DS1.GND, DS2.GND, Part3.GND, WATER_PUMP1.pin_1, KF-1.ground, AMS1.GND-_(output)
  N4: U1.D5, KF-1.signal
  VIN: U1.Vin, Part3.VCC, KF-1.power, KF-1.C, AMS1.VOUT+
  VCC: Part1.VCC, IC1.pin1, Part6.VDD, Part7.VCC
  GND_2: Part1.GND, IC1.pin2, Part6.GND, Part7.GND
  N5: Part1.AO, Part6.A1
  N6: Part1.POS, Part2.POS
  N7: Part1.NEG, Part2.NEG
  N8: WATER_PUMP1.pin_2, KF-1.NO
  N9: IC1.pin4, Part6.A2
  N10: Part6.A0, Part7.AO
  N11: AMS1.VIN+, VCC2.+
  N12: AMS1.GND-_(input), VCC2.-
  N13: Part7.POS, Part8.POS
  N14: Part7.NEG, Part8.NEG

custom parts:
  NodeMCU V1.0: ESP8266 based NodeMCU
  FC-28 Soil Hygrometer Module: The FC-28 is a soil hygrometer module that uses the Texas Instruments LM393 comparator chip to provide an analog measurement of soil humidity. The digital output is high when soil moisture is over a certain threshold, as determined by adjusting the potentiometer.
  FC-28 Soil Hygrometer Module - Probe: The FC-28 is a soil hygrometer module that uses the Texas Instruments LM393 comparator chip to provide an analog measurement of soil humidity.
  LCD1602-I2C: A standard character display, usually with 2x16 characters. Comes in many colors with LCM1602 IIC attached.
  water pump/motor: WATER PUMP BY ARDUBLOCKTR
  KF-301 Relay: KF-301
  MQ-2: MQ-2 Gas Sensor module
  ADS1115: ADC ADS1115
  AMS1777 5V regulator module: AMS1777 5V regulator module source : https://github.com/ShenTengTu/fritzing_parts/tree/master/voltage%20regulator/AMS1117_5V_regulator_module
  Battery: Your standard 2x 18650 battery pack (7.4 Volts)
