# Fritzing sketch 3 (saved by Fritzing 0.9.3b)

parts:
  U1 = NodeMCU V1.0
  DS1 = DS18B20 1-Wire Temperature Sensor Probe
  DS2 = DS18B20 1-Wire Temperature Sensor Probe
  Part1 = FC-28 Soil Hygrometer Module
  Part2 = FC-28 Soil Hygrometer Module - Probe
  WATER_PUMP1 = water pump/motor
  KF-1 = KF-301 Relay [package=THT]
  IC1 = MQ-2 [package="DIP (Dual Inline) [THT]"]
  Part6 = ADS1115
  Part7 = FC-28 Soil Hygrometer Module
  Part8 = FC-28 Soil Hygrometer Module - Probe
  R1 = Resistor [tolerance=±5% resistance=4.7k package="0402 [SMD]"]
  LCD2004-I2C1 = LCD2004-I2C
  BAT1 = 18650 battery holder [package=battery-18650-kit]
  Part9 = Solar Panel [package="Renogy 50 Watts 12 Volt Monocrystalline Bendable Solar Panel"]
  TP1 = TP4056 [chip_label=TP4056 package="DIP (Dual Inline) [THT]"]

nets:
  N1: U1.D1, Part6.SCL, LCD2004-I2C1.SCL
  N2: U1.D2, Part6.SDA, LCD2004-I2C1.SDA
  N3: U1.D4, DS1.DQ, DS2.DQ, R1.Pin_1
  VCC: U1.3V3, Part1.VCC, IC1.pin1, Part7.VCC
  GND: U1.GND, LCD2004-I2C1.GND
  N4: U1.D5, KF-1.signal
  VIN: U1.Vin, LCD2004-I2C1.VCC, TP1.pin3
  GND_2: DS1.GND, DS2.GND
  VDD: DS1.VDD, DS2.VDD, R1.Pin_0
  GND_3: Part1.GND, IC1.pin2, Part6.GND, Part7.GND
  N5: Part1.AO, Part6.A1
  N6: Part1.POS, Part2.POS
  N7: Part1.NEG, Part2.NEG
  N8: WATER_PUMP1.pin_2, KF-1.NO
  N9: KF-1.power, KF-1.C
  N10: IC1.pin4, Part6.A2
  N11: Part6.A0, Part7.AO
  N12: Part7.POS, Part8.POS
  N13: Part7.NEG, Part8.NEG
  N14: BAT1.+, TP1.pin5
  N15: BAT1.-, TP1.pin4
  N16: Part9.Connector_1, TP1.pin1
  N17: Part9.Connector_2, TP1.pin2

custom parts:
  NodeMCU V1.0: ESP8266 based NodeMCU
  FC-28 Soil Hygrometer Module: The FC-28 is a soil hygrometer module that uses the Texas Instruments LM393 comparator chip to provide an analog measurement of soil humidity. The digital output is high when soil moisture is over a certain threshold, as determined by adjusting the potentiometer.
  FC-28 Soil Hygrometer Module - Probe: The FC-28 is a soil hygrometer module that uses the Texas Instruments LM393 comparator chip to provide an analog measurement of soil humidity.
  water pump/motor: WATER PUMP BY ARDUBLOCKTR
  KF-301 Relay: KF-301
  MQ-2: MQ-2 Gas Sensor module
  ADS1115: ADC ADS1115
  LCD2004-I2C: A standard character display with 4x20 characters. Comes in many colors with LCM2004 IIC attached.
  18650 battery holder: 18650 Battery Holder identical to the dual battery version.
  Solar Panel: Renogy 50 Watts 12 Volt Solar Panel
  TP4056: A DIP stand-in part for whatever IC you want. With 6 pins on a 300mil dual inline package (DIP) footprint.
